# Fritzing sketch MIDTERM PROJECT (saved by Fritzing 0.9.3b)
breadboards: 1

parts:
  Part1 = Arduino Mega ADK (Rev3)
  R1 = Resistor [tolerance=±5% resistance=220 package=THT]
  R2 = Resistor [tolerance=±5% resistance=220 package=THT]
  R3 = Resistor [tolerance=±5% resistance=220 package=THT]
  R4 = Resistor [tolerance=±5% resistance=220 package=THT]
  R5 = Resistor [tolerance=±5% resistance=220 package=THT]
  R6 = Resistor [tolerance=±5% resistance=220 package=THT]

nets:
  N1: Part1.A0, R5.Pin_0, R6.Pin_0
  N2: Part1.A1, R3.Pin_0, R4.Pin_0
  N3: Part1.A2, R1.Pin_0, R2.Pin_0
  N4: Part1.5V, R1.Pin_1, R3.Pin_1, R5.Pin_1
  N5: Part1.GND, R2.Pin_1, R4.Pin_1, R6.Pin_1
